// Digital circuit CPU.dig as structural Verilog
module CPU (
  input  CLK,
  input  R_W,
  input  S0,
  input  S1,
  input  I0,
  input  I1,
  input  I2,
  input  I3,
  input  I4,
  input  I5,
  input  I6,
  input  I7,
  input  WRegB,
  input  WRegA,
  input  Sum_Substract,
  input  in_60,
  input  in_61,
  input  in_62,
  output Reg10,
  output Reg20,
  output Reg11,
  output Reg12,
  output Reg13,
  output Reg14,
  output Reg15,
  output Reg16,
  output Reg17,
  output Reg21,
  output Reg22,
  output Reg23,
  output Reg24,
  output Reg25,
  output Reg26,
  output Reg27,
  output Reg30,
  output Reg31,
  output Reg32,
  output Reg33,
  output Reg34,
  output Reg35,
  output Reg36,
  output Reg37,
  output Reg40,
  output Reg41,
  output Reg42,
  output Reg43,
  output Reg44,
  output Reg45,
  output Reg46,
  output Reg47,
  output Negative,
  output Carry_out,
  output Zero,
  output Overflow,
  output Y0,
  output Y1,
  output Y2,
  output Y3,
  output Y4,
  output Y5,
  output Y6,
  output Y7
);

  wire demultiplexor_1_y0, demultiplexor_1_y1, demultiplexor_1_y2, demultiplexor_1_y3, flipflop_8bit_5_y0,
       flipflop_8bit_5_y1, flipflop_8bit_5_y2, flipflop_8bit_5_y3, flipflop_8bit_5_y4, flipflop_8bit_5_y5,
       flipflop_8bit_5_y6, flipflop_8bit_5_y7, flipflop_8bit_6_y0, flipflop_8bit_6_y1, flipflop_8bit_6_y2,
       flipflop_8bit_6_y3, flipflop_8bit_6_y4, flipflop_8bit_6_y5, flipflop_8bit_6_y6, flipflop_8bit_6_y7,
       flipflop_8bit_7_y0, flipflop_8bit_7_y1, flipflop_8bit_7_y2, flipflop_8bit_7_y3, flipflop_8bit_7_y4,
       flipflop_8bit_7_y5, flipflop_8bit_7_y6, flipflop_8bit_7_y7, multiplexor_4_1_y, multiplexor_4_2_y,
       multiplexor_4_3_y, multiplexor_4_4_y, multiplexor_4_5_y, multiplexor_4_6_y, multiplexor_4_7_y,
       multiplexor_4_8_y, not_1_out, undriven, undriven_2, undriven_3, undriven_4, undriven_5, undriven_6,
       undriven_7, undriven_8;

  TriState_Switch tristate_switch_1 (
    .Y0(Y0), .Y1(Y1), .Y2(Y2), .Y3(Y3), .Y4(Y4), .Y5(Y5), .Y6(Y6), .Y7(Y7), .I0(I0), .I1(I1), .I2(I2),
    .I3(I3), .I4(I4), .I5(I5), .I6(I6), .I7(I7), .Enable(in_60));
  Demultiplexor demultiplexor_1 (
    .S0(S0), .S1(S1), .I(R_W), .Y0(demultiplexor_1_y0), .Y1(demultiplexor_1_y1), .Y2(demultiplexor_1_y2),
    .Y3(demultiplexor_1_y3));
  Flipflop_8bit flipflop_8bit_1 (
    .Y0(Reg10), .Y1(Reg11), .Y2(Reg12), .Y3(Reg13), .Y4(Reg14), .Y5(Reg15), .Y6(Reg16), .Y7(Reg17),
    .CLK(CLK), .EN(demultiplexor_1_y0), .D0(Y0), .D1(Y1), .D2(Y2), .D3(Y3), .D4(Y4), .D5(Y5), .D6(Y6), .D7(Y7));
  Flipflop_8bit flipflop_8bit_2 (
    .Y0(Reg20), .Y1(Reg21), .Y2(Reg22), .Y3(Reg23), .Y4(Reg24), .Y5(Reg25), .Y6(Reg26), .Y7(Reg27),
    .CLK(CLK), .EN(demultiplexor_1_y1), .D0(Y0), .D1(Y1), .D2(Y2), .D3(Y3), .D4(Y4), .D5(Y5), .D6(Y6), .D7(Y7));
  Flipflop_8bit flipflop_8bit_3 (
    .Y0(Reg30), .Y1(Reg31), .Y2(Reg32), .Y3(Reg33), .Y4(Reg34), .Y5(Reg25), .Y6(Reg36), .Y7(Reg37),
    .CLK(CLK), .EN(demultiplexor_1_y2), .D0(Y0), .D1(Y1), .D2(Y2), .D3(Y3), .D4(Y4), .D5(Y5), .D6(Y6), .D7(Y7));
  Flipflop_8bit flipflop_8bit_4 (
    .Y0(Reg40), .Y1(Reg41), .Y2(Reg42), .Y3(Reg43), .Y4(Reg44), .Y5(Reg45), .Y6(Reg46), .Y7(Reg47),
    .CLK(CLK), .EN(demultiplexor_1_y3), .D0(Y0), .D1(Y1), .D2(Y2), .D3(Y3), .D4(Y4), .D5(Y5), .D6(Y6), .D7(Y7));
  Multiplexor_4 multiplexor_4_1 (
    .Y(multiplexor_4_1_y), .I0(Reg10), .I1(Reg20), .I2(Reg30), .I3(Reg40), .S0(S0), .S1(S1));
  not not_1 (not_1_out, R_W);
  Multiplexor_4 multiplexor_4_2 (
    .Y(multiplexor_4_2_y), .I0(Reg11), .I1(Reg21), .I2(Reg31), .I3(Reg41), .S0(S0), .S1(S1));
  Multiplexor_4 multiplexor_4_3 (
    .Y(multiplexor_4_3_y), .I0(Reg12), .I1(Reg22), .I2(Reg32), .I3(Reg42), .S0(S0), .S1(S1));
  TriState_Switch tristate_switch_2 (
    .Y0(Y0), .Y1(Y1), .Y2(Y2), .Y3(Y3), .Y4(Y4), .Y5(Y5), .Y6(Y6), .Y7(Y7), .I0(flipflop_8bit_5_y0),
    .I1(flipflop_8bit_5_y1), .I2(flipflop_8bit_5_y2), .I3(flipflop_8bit_5_y3), .I4(flipflop_8bit_5_y4),
    .I5(flipflop_8bit_5_y5), .I6(flipflop_8bit_5_y6), .I7(flipflop_8bit_5_y7), .Enable(in_62));
  Flipflop_8bit flipflop_8bit_5 (
    .Y0(flipflop_8bit_5_y0), .Y1(flipflop_8bit_5_y1), .Y2(flipflop_8bit_5_y2), .Y3(flipflop_8bit_5_y3),
    .Y4(flipflop_8bit_5_y4), .Y5(flipflop_8bit_5_y5), .Y6(flipflop_8bit_5_y6), .Y7(flipflop_8bit_5_y7),
    .CLK(CLK), .EN(not_1_out), .D0(multiplexor_4_1_y), .D1(multiplexor_4_2_y), .D2(multiplexor_4_3_y),
    .D3(multiplexor_4_4_y), .D4(multiplexor_4_5_y), .D5(multiplexor_4_6_y), .D6(multiplexor_4_7_y),
    .D7(multiplexor_4_8_y));
  Multiplexor_4 multiplexor_4_4 (
    .Y(multiplexor_4_4_y), .I0(Reg13), .I1(Reg23), .I2(Reg33), .I3(Reg43), .S0(S0), .S1(S1));
  Multiplexor_4 multiplexor_4_5 (
    .Y(multiplexor_4_5_y), .I0(Reg14), .I1(Reg24), .I2(Reg34), .I3(Reg44), .S0(S0), .S1(S1));
  Multiplexor_4 multiplexor_4_6 (
    .Y(multiplexor_4_6_y), .I0(Reg15), .I1(Reg25), .I2(Reg25), .I3(Reg45), .S0(S0), .S1(S1));
  Multiplexor_4 multiplexor_4_7 (
    .Y(multiplexor_4_7_y), .I0(Reg16), .I1(Reg26), .I2(Reg36), .I3(Reg46), .S0(S0), .S1(S1));
  Multiplexor_4 multiplexor_4_8 (
    .Y(multiplexor_4_8_y), .I0(Reg17), .I1(Reg27), .I2(Reg37), .I3(Reg47), .S0(S0), .S1(S1));
  Flipflop_8bit flipflop_8bit_6 (
    .Y0(flipflop_8bit_6_y0), .Y1(flipflop_8bit_6_y1), .Y2(flipflop_8bit_6_y2), .Y3(flipflop_8bit_6_y3),
    .Y4(flipflop_8bit_6_y4), .Y5(flipflop_8bit_6_y5), .Y6(flipflop_8bit_6_y6), .Y7(flipflop_8bit_6_y7),
    .CLK(WRegA), .EN(1'b1), .D0(Y0), .D1(Y1), .D2(Y2), .D3(Y3), .D4(Y4), .D5(Y5), .D6(Y6), .D7(Y7));
  Flipflop_8bit flipflop_8bit_7 (
    .Y0(flipflop_8bit_7_y0), .Y1(flipflop_8bit_7_y1), .Y2(flipflop_8bit_7_y2), .Y3(flipflop_8bit_7_y3),
    .Y4(flipflop_8bit_7_y4), .Y5(flipflop_8bit_7_y5), .Y6(flipflop_8bit_7_y6), .Y7(flipflop_8bit_7_y7),
    .CLK(WRegB), .EN(1'b1), .D0(Y0), .D1(Y1), .D2(Y2), .D3(Y3), .D4(Y4), .D5(Y5), .D6(Y6), .D7(Y7));
  ALU alu_1 ();
  TriState_Switch tristate_switch_3 (
    .Y0(Y0), .Y1(Y1), .Y2(Y2), .Y3(Y3), .Y4(Y4), .Y5(Y5), .Y6(Y6), .Y7(Y7), .I0(undriven_8), .I1(undriven_7),
    .I2(undriven_5), .I3(undriven_6), .I4(undriven), .I5(undriven_2), .I6(undriven_3), .I7(undriven_4),
    .Enable(in_61));

  assign Reg35 = Reg25;
endmodule
