// Digital circuit D_FlipFLop_BothEdges.dig as structural Verilog
module D_FlipFLop_BothEdges (
  input  D,
  input  CLK,
  output Y
);

  wire multiplexor_2_1_y, multiplexor_2_2_y, multiplexor_2_3_y, multiplexor_2_4_y, not_1_out;

  not not_1 (not_1_out, CLK);
  Multiplexor_2 multiplexor_2_1 (.A(multiplexor_2_1_y), .B(D), .S(CLK), .Y(multiplexor_2_1_y));
  Multiplexor_2 multiplexor_2_2 (.A(multiplexor_2_2_y), .B(D), .S(not_1_out), .Y(multiplexor_2_2_y));
  Multiplexor_2 multiplexor_2_3 (.A(multiplexor_2_3_y), .B(multiplexor_2_1_y), .S(not_1_out), .Y(multiplexor_2_3_y));
  Multiplexor_2 multiplexor_2_4 (.A(multiplexor_2_4_y), .B(multiplexor_2_2_y), .S(CLK), .Y(multiplexor_2_4_y));
  Multiplexor_2 multiplexor_2_5 (.A(multiplexor_2_3_y), .B(multiplexor_2_4_y), .S(CLK), .Y(Y));
endmodule
