// Digital circuit D_FlipFlop_Enable.dig as structural Verilog
module D_FlipFlop_Enable (
  input  D,
  input  CLK,
  input  Enable,
  output Y
);

  wire multiplexor_2_1_y, multiplexor_2_2_y, not_1_out;

  Multiplexor_2 multiplexor_2_1 (.A(Y), .B(D), .S(Enable), .Y(multiplexor_2_1_y));
  not not_1 (not_1_out, CLK);
  Multiplexor_2 multiplexor_2_2 (.A(multiplexor_2_2_y), .B(multiplexor_2_1_y), .S(not_1_out), .Y(multiplexor_2_2_y));
  Multiplexor_2 multiplexor_2_3 (.A(Y), .B(multiplexor_2_2_y), .S(CLK), .Y(Y));
endmodule
