// Digital circuit D_FlipFlop_FallingEdge.dig as structural Verilog
module D_FlipFlop_FallingEdge (
  input  D,
  input  CLK,
  output Q,
  output Q_2
);

  wire and_1_out, and_2_out, and_3_out, and_4_out, not_1_out, not_2_out, rs_nor_latch_1_q, rs_nor_latch_1_q_2;

  not not_1 (not_1_out, D);
  and and_1 (and_1_out, not_1_out, CLK);
  and and_2 (and_2_out, D, CLK);
  not not_2 (not_2_out, CLK);
  RS_NOR_LATCH rs_nor_latch_1 (.R(and_1_out), .S(and_2_out), .Q(rs_nor_latch_1_q), .Q_2(rs_nor_latch_1_q_2));
  and and_3 (and_3_out, rs_nor_latch_1_q, not_2_out);
  and and_4 (and_4_out, rs_nor_latch_1_q_2, not_2_out);
  RS_NOR_LATCH rs_nor_latch_2 (.R(and_4_out), .S(and_3_out), .Q(Q), .Q_2(Q_2));
endmodule
