// Digital circuit D_FlipFlop_RaisingEdge.dig as structural Verilog
module D_FlipFlop_RaisingEdge (
  input  D,
  input  CLK,
  output Y
);

  wire multiplexor_2_1_y, not_1_out;

  not not_1 (not_1_out, CLK);
  Multiplexor_2 multiplexor_2_1 (.A(multiplexor_2_1_y), .B(D), .S(not_1_out), .Y(multiplexor_2_1_y));
  Multiplexor_2 multiplexor_2_2 (.A(Y), .B(multiplexor_2_1_y), .S(CLK), .Y(Y));
endmodule
