// Digital circuit Demultiplexor.dig as structural Verilog
module Demultiplexor (
  input  S0,
  input  S1,
  input  I0,
  output Y0,
  output Y1,
  output Y2,
  output Y3
);

  wire and_1_out, and_2_out, and_3_out, and_4_out, and_5_out, and_6_out, and_7_out, and_8_out, not_1_out,
       not_2_out;

  not not_1 (not_1_out, S0);
  not not_2 (not_2_out, S1);
  and and_1 (and_1_out, not_2_out, I0);
  and and_2 (and_2_out, not_1_out, I0);
  and and_3 (and_3_out, S0, I0);
  and and_4 (and_4_out, not_2_out, I0);
  and and_5 (and_5_out, S1, I0);
  and and_6 (and_6_out, not_1_out, I0);
  and and_7 (and_7_out, S1, I0);
  and and_8 (and_8_out, S0, I0);
  and and_9 (Y0, and_1_out, and_2_out);
  and and_10 (Y1, and_3_out, and_4_out);
  and and_11 (Y2, and_5_out, and_6_out);
  and and_12 (Y3, and_7_out, and_8_out);
endmodule
