// Digital circuit FULL_ALU.dig as structural Verilog
module FULL_ALU (
  input  A0,
  input  A1,
  input  A2,
  input  A3,
  input  A4,
  input  A5,
  input  A6,
  input  A7,
  input  B0,
  input  B1,
  input  B2,
  input  B3,
  input  B4,
  input  B5,
  input  B6,
  input  B7,
  input  ALU_OUT,
  input  S0,
  input  S1,
  input  S2,
  output Y0,
  output Y1,
  output Y2,
  output Y3,
  output Y4,
  output Y5,
  output Y6,
  output Y7,
  output Overflow,
  output Zero,
  output Carry_Out,
  output Negative
);

  wire and_1_out, and_2_out, and_3_out, and_4_out, and_5_out, and_6_out, and_7_out, and_8_out,
       full_adder_1_carry_out, full_adder_1_y, full_adder_2_carry_out, full_adder_2_y,
       full_adder_3_carry_out, full_adder_3_y, full_adder_4_carry_out, full_adder_4_y,
       full_adder_5_carry_out, full_adder_5_y, full_adder_6_carry_out, full_adder_6_y,
       full_adder_7_carry_out, full_adder_7_y, full_adder_8_y, multiplexor_2_8bits_1_y0,
       multiplexor_2_8bits_1_y1, multiplexor_2_8bits_1_y2, multiplexor_2_8bits_1_y3,
       multiplexor_2_8bits_1_y4, multiplexor_2_8bits_1_y5, multiplexor_2_8bits_1_y6,
       multiplexor_2_8bits_1_y7, multiplexor_2_8bits_2_y0, multiplexor_2_8bits_2_y1,
       multiplexor_2_8bits_2_y2, multiplexor_2_8bits_2_y3, multiplexor_2_8bits_2_y4,
       multiplexor_2_8bits_2_y5, multiplexor_2_8bits_2_y6, multiplexor_2_8bits_2_y7,
       multiplexor_2_8bits_3_y0, multiplexor_2_8bits_3_y1, multiplexor_2_8bits_3_y2,
       multiplexor_2_8bits_3_y3, multiplexor_2_8bits_3_y4, multiplexor_2_8bits_3_y5,
       multiplexor_2_8bits_3_y6, multiplexor_2_8bits_3_y7, multiplexor_2_8bits_4_y0,
       multiplexor_2_8bits_4_y1, multiplexor_2_8bits_4_y2, multiplexor_2_8bits_4_y3,
       multiplexor_2_8bits_4_y4, multiplexor_2_8bits_4_y5, multiplexor_2_8bits_4_y6,
       multiplexor_2_8bits_4_y7, multiplexor_2_8bits_5_y0, multiplexor_2_8bits_5_y1,
       multiplexor_2_8bits_5_y2, multiplexor_2_8bits_5_y3, multiplexor_2_8bits_5_y4,
       multiplexor_2_8bits_5_y5, multiplexor_2_8bits_5_y6, multiplexor_2_8bits_5_y7,
       multiplexor_2_8bits_6_y0, multiplexor_2_8bits_6_y1, multiplexor_2_8bits_6_y2,
       multiplexor_2_8bits_6_y3, multiplexor_2_8bits_6_y4, multiplexor_2_8bits_6_y5,
       multiplexor_2_8bits_6_y6, multiplexor_2_8bits_6_y7, or_1_out, or_2_out, or_3_out, or_4_out, or_5_out,
       or_6_out, or_7_out, or_8_out, or_9_out, or_10_out, xor_1_out, xor_2_out, xor_3_out, xor_4_out,
       xor_5_out, xor_6_out, xor_7_out, xor_8_out, xor_9_out, xor_10_out, xor_11_out, xor_12_out, xor_13_out,
       xor_14_out, xor_15_out, xor_16_out;

  xor xor_1 (xor_1_out, B0, A0);
  xor xor_2 (xor_2_out, B1, A1);
  xor xor_3 (xor_3_out, B2, A2);
  xor xor_4 (xor_4_out, B3, A3);
  xor xor_5 (xor_5_out, B4, A4);
  xor xor_6 (xor_6_out, B5, A5);
  xor xor_7 (xor_7_out, B6, A6);
  xor xor_8 (xor_8_out, B7, A7);
  or or_1 (or_1_out, A0, B0);
  or or_2 (or_2_out, B1, A1);
  or or_3 (or_3_out, B2, A2);
  or or_4 (or_4_out, B3, A3);
  or or_5 (or_5_out, B4, A4);
  or or_6 (or_6_out, B5, A5);
  or or_7 (or_7_out, B6, A6);
  or or_8 (or_8_out, A7, B7);
  and and_1 (and_1_out, A0, B0);
  and and_2 (and_2_out, A1, B1);
  Multiplexor_2_8bits multiplexor_2_8bits_1 (
    .A0(1'b0), .B0(A1), .A1(A0), .B1(A2), .A2(A1), .B2(A3), .A3(A2), .B3(A4), .A4(A3), .B4(A5), .A5(A4),
    .B5(A6), .A6(A5), .B6(A7), .A7(A6), .B7(1'b0), .Y0(multiplexor_2_8bits_1_y0),
    .Y1(multiplexor_2_8bits_1_y1), .Y2(multiplexor_2_8bits_1_y2), .Y3(multiplexor_2_8bits_1_y3),
    .Y4(multiplexor_2_8bits_1_y4), .Y5(multiplexor_2_8bits_1_y5), .Y6(multiplexor_2_8bits_1_y6),
    .Y7(multiplexor_2_8bits_1_y7), .S0(S0));
  and and_3 (and_3_out, A2, B2);
  and and_4 (and_4_out, A3, B3);
  and and_5 (and_5_out, A4, B4);
  and and_6 (and_6_out, B5, A5);
  and and_7 (and_7_out, A6, B6);
  and and_8 (and_8_out, A7, B7);
  Multiplexor_2_8bits multiplexor_2_8bits_2 (
    .A0(and_1_out), .B0(or_1_out), .A1(and_2_out), .B1(or_2_out), .A2(and_3_out), .B2(or_3_out),
    .A3(and_4_out), .B3(or_4_out), .A4(and_5_out), .B4(or_5_out), .A5(and_6_out), .B5(or_6_out),
    .A6(and_7_out), .B6(or_7_out), .A7(and_8_out), .B7(or_8_out), .Y0(multiplexor_2_8bits_2_y0),
    .Y1(multiplexor_2_8bits_2_y1), .Y2(multiplexor_2_8bits_2_y2), .Y3(multiplexor_2_8bits_2_y3),
    .Y4(multiplexor_2_8bits_2_y4), .Y5(multiplexor_2_8bits_2_y5), .Y6(multiplexor_2_8bits_2_y6),
    .Y7(multiplexor_2_8bits_2_y7), .S0(S0));
  Multiplexor_2_8bits multiplexor_2_8bits_3 (
    .A0(xor_1_out), .B0(A1), .A1(xor_2_out), .B1(A2), .A2(xor_3_out), .B2(A3), .A3(xor_4_out), .B3(A4),
    .A4(xor_5_out), .B4(A5), .A5(xor_6_out), .B5(A6), .A6(xor_7_out), .B6(A7), .A7(xor_8_out), .B7(A7),
    .Y0(multiplexor_2_8bits_3_y0), .Y1(multiplexor_2_8bits_3_y1), .Y2(multiplexor_2_8bits_3_y2),
    .Y3(multiplexor_2_8bits_3_y3), .Y4(multiplexor_2_8bits_3_y4), .Y5(multiplexor_2_8bits_3_y5),
    .Y6(multiplexor_2_8bits_3_y6), .Y7(multiplexor_2_8bits_3_y7), .S0(S0));
  xor xor_9 (xor_9_out, S0, B0);
  xor xor_10 (xor_10_out, S0, B1);
  xor xor_11 (xor_11_out, S0, B2);
  xor xor_12 (xor_12_out, S0, B3);
  xor xor_13 (xor_13_out, S0, B4);
  xor xor_14 (xor_14_out, S0, B5);
  xor xor_15 (xor_15_out, S0, B6);
  xor xor_16 (xor_16_out, S0, B7);
  Multiplexor_2_8bits multiplexor_2_8bits_4 (
    .A0(multiplexor_2_8bits_3_y0), .B0(multiplexor_2_8bits_1_y0), .A1(multiplexor_2_8bits_3_y1),
    .B1(multiplexor_2_8bits_1_y1), .A2(multiplexor_2_8bits_3_y2), .B2(multiplexor_2_8bits_1_y2),
    .A3(multiplexor_2_8bits_3_y3), .B3(multiplexor_2_8bits_1_y3), .A4(multiplexor_2_8bits_3_y4),
    .B4(multiplexor_2_8bits_1_y4), .A5(multiplexor_2_8bits_3_y5), .B5(multiplexor_2_8bits_1_y5),
    .A6(multiplexor_2_8bits_3_y6), .B6(multiplexor_2_8bits_1_y6), .A7(multiplexor_2_8bits_3_y7),
    .B7(multiplexor_2_8bits_1_y7), .Y0(multiplexor_2_8bits_4_y0), .Y1(multiplexor_2_8bits_4_y1),
    .Y2(multiplexor_2_8bits_4_y2), .Y3(multiplexor_2_8bits_4_y3), .Y4(multiplexor_2_8bits_4_y4),
    .Y5(multiplexor_2_8bits_4_y5), .Y6(multiplexor_2_8bits_4_y6), .Y7(multiplexor_2_8bits_4_y7), .S0(S1));
  Full_Adder full_adder_1 (
    .Carry_In(S0), .A(A0), .B(xor_9_out), .Y(full_adder_1_y), .Carry_out(full_adder_1_carry_out));
  Full_Adder full_adder_2 (
    .Carry_In(full_adder_1_carry_out), .A(A1), .B(xor_10_out), .Y(full_adder_2_y),
    .Carry_out(full_adder_2_carry_out));
  Full_Adder full_adder_3 (
    .Carry_In(full_adder_2_carry_out), .A(A2), .B(xor_11_out), .Y(full_adder_3_y),
    .Carry_out(full_adder_3_carry_out));
  Full_Adder full_adder_4 (
    .Carry_In(full_adder_3_carry_out), .A(A3), .B(xor_12_out), .Y(full_adder_4_y),
    .Carry_out(full_adder_4_carry_out));
  Full_Adder full_adder_5 (
    .Carry_In(full_adder_4_carry_out), .A(A4), .B(xor_13_out), .Y(full_adder_5_y),
    .Carry_out(full_adder_5_carry_out));
  Full_Adder full_adder_6 (
    .Carry_In(full_adder_5_carry_out), .A(A5), .B(xor_14_out), .Y(full_adder_6_y),
    .Carry_out(full_adder_6_carry_out));
  Full_Adder full_adder_7 (
    .Carry_In(full_adder_6_carry_out), .A(A6), .B(xor_15_out), .Y(full_adder_7_y),
    .Carry_out(full_adder_7_carry_out));
  Full_Adder full_adder_8 (
    .Carry_In(full_adder_7_carry_out), .A(A7), .B(xor_16_out), .Y(full_adder_8_y), .Carry_out(Carry_Out));
  xor xor_17 (Overflow, Carry_Out, full_adder_7_carry_out);
  Multiplexor_2_8bits multiplexor_2_8bits_5 (
    .A0(full_adder_1_y), .B0(multiplexor_2_8bits_2_y0), .A1(full_adder_2_y), .B1(multiplexor_2_8bits_2_y1),
    .A2(full_adder_3_y), .B2(multiplexor_2_8bits_2_y2), .A3(full_adder_4_y), .B3(multiplexor_2_8bits_2_y3),
    .A4(full_adder_5_y), .B4(multiplexor_2_8bits_2_y4), .A5(full_adder_6_y), .B5(multiplexor_2_8bits_2_y5),
    .A6(full_adder_7_y), .B6(multiplexor_2_8bits_2_y6), .A7(full_adder_8_y), .B7(multiplexor_2_8bits_2_y7),
    .Y0(multiplexor_2_8bits_5_y0), .Y1(multiplexor_2_8bits_5_y1), .Y2(multiplexor_2_8bits_5_y2),
    .Y3(multiplexor_2_8bits_5_y3), .Y4(multiplexor_2_8bits_5_y4), .Y5(multiplexor_2_8bits_5_y5),
    .Y6(multiplexor_2_8bits_5_y6), .Y7(multiplexor_2_8bits_5_y7), .S0(S1));
  Multiplexor_2_8bits multiplexor_2_8bits_6 (
    .A0(multiplexor_2_8bits_5_y0), .B0(multiplexor_2_8bits_4_y0), .A1(multiplexor_2_8bits_5_y1),
    .B1(multiplexor_2_8bits_4_y1), .A2(multiplexor_2_8bits_5_y2), .B2(multiplexor_2_8bits_4_y2),
    .A3(multiplexor_2_8bits_5_y3), .B3(multiplexor_2_8bits_4_y3), .A4(multiplexor_2_8bits_5_y4),
    .B4(multiplexor_2_8bits_4_y4), .A5(multiplexor_2_8bits_5_y5), .B5(multiplexor_2_8bits_4_y5),
    .A6(multiplexor_2_8bits_5_y6), .B6(multiplexor_2_8bits_4_y6), .A7(multiplexor_2_8bits_5_y7),
    .B7(multiplexor_2_8bits_4_y7), .Y0(multiplexor_2_8bits_6_y0), .Y1(multiplexor_2_8bits_6_y1),
    .Y2(multiplexor_2_8bits_6_y2), .Y3(multiplexor_2_8bits_6_y3), .Y4(multiplexor_2_8bits_6_y4),
    .Y5(multiplexor_2_8bits_6_y5), .Y6(multiplexor_2_8bits_6_y6), .Y7(multiplexor_2_8bits_6_y7), .S0(S2));
  TriState_Switch tristate_switch_1 (
    .Y0(Y0), .Y1(Y1), .Y2(Y2), .Y3(Y3), .Y4(Y4), .Y5(Y5), .Y6(Y6), .Y7(Negative),
    .I0(multiplexor_2_8bits_6_y0), .I1(multiplexor_2_8bits_6_y1), .I2(multiplexor_2_8bits_6_y2),
    .I3(multiplexor_2_8bits_6_y3), .I4(multiplexor_2_8bits_6_y4), .I5(multiplexor_2_8bits_6_y5),
    .I6(multiplexor_2_8bits_6_y6), .I7(multiplexor_2_8bits_6_y7), .Enable(ALU_OUT));
  or or_9 (or_9_out, Y4, Y5, Y6, Negative);
  nor nor_1 (Zero, or_10_out, or_9_out);
  or or_10 (or_10_out, Y0, Y1, Y2, Y3);

  assign Y7 = Negative;

  // Notes on the sheet:
  //   000 ----> Add
  //   001 ----> Substract
  //   010  -----> AND	
  //   011 -------> OR
  //   100   -------> XOR
  //   101 ---------> ASR
  //   110 ----------> LSL
  //   111 ----------> LSR
endmodule
