// Digital circuit Flipflop_8bit.dig as structural Verilog
module Flipflop_8bit (
  input  CLK,
  input  EN,
  input  D0,
  input  D1,
  input  D2,
  input  D3,
  input  D4,
  input  D5,
  input  D6,
  input  D7,
  output Y0,
  output Y1,
  output Y2,
  output Y3,
  output Y4,
  output Y5,
  output Y6,
  output Y7
);

  D_FlipFlop_Enable d_flipflop_enable_1 (.D(D0), .CLK(CLK), .Enable(EN), .Y(Y0));
  D_FlipFlop_Enable d_flipflop_enable_2 (.D(D1), .CLK(CLK), .Enable(EN), .Y(Y1));
  D_FlipFlop_Enable d_flipflop_enable_3 (.D(D2), .CLK(CLK), .Enable(EN), .Y(Y2));
  D_FlipFlop_Enable d_flipflop_enable_4 (.D(D3), .CLK(CLK), .Enable(EN), .Y(Y3));
  D_FlipFlop_Enable d_flipflop_enable_5 (.D(D4), .CLK(CLK), .Enable(EN), .Y(Y4));
  D_FlipFlop_Enable d_flipflop_enable_6 (.D(D5), .CLK(CLK), .Enable(EN), .Y(Y5));
  D_FlipFlop_Enable d_flipflop_enable_7 (.D(D6), .CLK(CLK), .Enable(EN), .Y(Y6));
  D_FlipFlop_Enable d_flipflop_enable_8 (.D(D7), .CLK(CLK), .Enable(EN), .Y(Y7));
endmodule
