// Digital circuit Full_Adder.dig as structural Verilog
module Full_Adder (
  input  Carry_In,
  input  A,
  input  B,
  output Y,
  output Carry_out
);

  wire and_1_out, and_2_out, xor_1_out;

  xor xor_1 (xor_1_out, Carry_In, A);
  xor xor_2 (Y, xor_1_out, B);
  and and_1 (and_1_out, Carry_In, A);
  and and_2 (and_2_out, xor_1_out, B);
  or or_1 (Carry_out, and_1_out, and_2_out);
endmodule
