// Digital circuit Multiplexor_2.dig as structural Verilog
module Multiplexor_2 (
  input  A,
  input  B,
  input  S,
  output Y
);

  wire and_1_out, and_2_out, and_3_out, not_1_out;

  not not_1 (not_1_out, S);
  and and_1 (and_1_out, A, not_1_out);
  and and_2 (and_2_out, B, S);
  and and_3 (and_3_out, B, A);
  or or_1 (Y, and_1_out, and_3_out, and_2_out);
endmodule
