// Digital circuit Multiplexor_2_8bits.dig as structural Verilog
module Multiplexor_2_8bits (
  input  A0,
  input  A1,
  input  A2,
  input  A3,
  input  A4,
  input  A5,
  input  A6,
  input  A7,
  input  S0,
  input  B0,
  input  B1,
  input  B2,
  input  B3,
  input  B4,
  input  B5,
  input  B6,
  input  B7,
  output Y0,
  output Y1,
  output Y2,
  output Y3,
  output Y4,
  output Y5,
  output Y6,
  output Y7
);

  Multiplexor_2 multiplexor_2_1 (.A(A0), .B(B0), .S(S0), .Y(Y0));
  Multiplexor_2 multiplexor_2_2 (.A(A1), .B(B1), .S(S0), .Y(Y1));
  Multiplexor_2 multiplexor_2_3 (.A(A2), .B(B2), .S(S0), .Y(Y2));
  Multiplexor_2 multiplexor_2_4 (.A(A3), .B(B3), .S(S0), .Y(Y3));
  Multiplexor_2 multiplexor_2_5 (.A(A4), .B(B4), .S(S0), .Y(Y4));
  Multiplexor_2 multiplexor_2_6 (.A(A5), .B(B5), .S(S0), .Y(Y5));
  Multiplexor_2 multiplexor_2_7 (.A(A6), .B(B6), .S(S0), .Y(Y6));
  Multiplexor_2 multiplexor_2_8 (.A(A7), .B(B7), .S(S0), .Y(Y7));
endmodule
