// Digital circuit Multiplexor_4.dig as structural Verilog
module Multiplexor_4 (
  input  I0,
  input  I1,
  input  I2,
  input  I3,
  input  S0,
  input  S1,
  output Y
);

  wire multiplexor_2_1_y, multiplexor_2_2_y;

  Multiplexor_2 multiplexor_2_1 (.A(I0), .B(I1), .S(S0), .Y(multiplexor_2_1_y));
  Multiplexor_2 multiplexor_2_2 (.A(I2), .B(I3), .S(S0), .Y(multiplexor_2_2_y));
  Multiplexor_2 multiplexor_2_3 (.A(multiplexor_2_1_y), .B(multiplexor_2_2_y), .S(S1), .Y(Y));
endmodule
