// Digital circuit OR.dig as structural Verilog
module OR (
  input  A,
  input  B,
  output Y
);

  wire and_using_nand_1_p3, nand_1_out, nand_2_out, nand_3_out;

  nand nand_1 (nand_1_out, A, A);
  nand nand_2 (nand_2_out, A, B);
  nand nand_3 (nand_3_out, B, B);
  // And_using_Nand and_using_nand_1: pin names not known; wires that end beside it: nand_1_out, nand_3_out, and_using_nand_1_p3
  nand nand_4 (Y, nand_2_out, and_using_nand_1_p3);
endmodule
