// Digital circuit PC_Counter.dig as structural Verilog
module PC_Counter (
  input  PC_OUT,
  input  PC_inc,
  input  PC_load,
  input  Reset,
  input  CLK,
  input  Din0,
  input  Din1,
  input  Din2,
  input  Din3,
  input  Din4,
  input  Din5,
  input  Din6,
  input  Din7,
  output Y0,
  output Y1,
  output Y2,
  output Y3,
  output Y4,
  output Y5,
  output Y6,
  output Y7,
  output Zero
);

  wire and_1_out, and_2_out, and_3_out, and_4_out, and_5_out, and_6_out, and_7_out, and_8_out, and_9_out,
       flipflop_8bit_1_y0, flipflop_8bit_1_y1, flipflop_8bit_1_y2, flipflop_8bit_1_y3, flipflop_8bit_1_y4,
       flipflop_8bit_1_y5, flipflop_8bit_1_y6, flipflop_8bit_1_y7, full_adder_1_carry_out, full_adder_1_y,
       full_adder_2_carry_out, full_adder_2_y, full_adder_3_carry_out, full_adder_3_y,
       full_adder_4_carry_out, full_adder_4_y, full_adder_5_carry_out, full_adder_5_y,
       full_adder_6_carry_out, full_adder_6_y, full_adder_7_carry_out, full_adder_7_y, full_adder_8_y,
       multiplexor_2_8bits_1_y0, multiplexor_2_8bits_1_y1, multiplexor_2_8bits_1_y2,
       multiplexor_2_8bits_1_y3, multiplexor_2_8bits_1_y4, multiplexor_2_8bits_1_y5,
       multiplexor_2_8bits_1_y6, multiplexor_2_8bits_1_y7, not_1_out, not_2_out, or_1_out, or_2_out, or_3_out;

  or or_1 (or_1_out, Reset, PC_load);
  not not_1 (not_1_out, or_1_out);
  and and_1 (and_1_out, not_1_out, PC_inc);
  not not_2 (not_2_out, Reset);
  Full_Adder full_adder_1 (
    .Carry_In(1'b0), .A(and_1_out), .B(flipflop_8bit_1_y0), .Y(full_adder_1_y),
    .Carry_out(full_adder_1_carry_out));
  Full_Adder full_adder_2 (
    .Carry_In(full_adder_1_carry_out), .A(1'b0), .B(flipflop_8bit_1_y1), .Y(full_adder_2_y),
    .Carry_out(full_adder_2_carry_out));
  Full_Adder full_adder_3 (
    .Carry_In(full_adder_2_carry_out), .A(1'b0), .B(flipflop_8bit_1_y2), .Y(full_adder_3_y),
    .Carry_out(full_adder_3_carry_out));
  Full_Adder full_adder_4 (
    .Carry_In(full_adder_3_carry_out), .A(1'b0), .B(flipflop_8bit_1_y3), .Y(full_adder_4_y),
    .Carry_out(full_adder_4_carry_out));
  Full_Adder full_adder_5 (
    .Carry_In(full_adder_4_carry_out), .A(1'b0), .B(flipflop_8bit_1_y4), .Y(full_adder_5_y),
    .Carry_out(full_adder_5_carry_out));
  Full_Adder full_adder_6 (
    .Carry_In(full_adder_5_carry_out), .A(1'b0), .B(flipflop_8bit_1_y5), .Y(full_adder_6_y),
    .Carry_out(full_adder_6_carry_out));
  Full_Adder full_adder_7 (
    .Carry_In(full_adder_6_carry_out), .A(1'b0), .B(flipflop_8bit_1_y6), .Y(full_adder_7_y),
    .Carry_out(full_adder_7_carry_out));
  Full_Adder full_adder_8 (
    .Carry_In(full_adder_7_carry_out), .A(1'b0), .B(flipflop_8bit_1_y7), .Y(full_adder_8_y));  // open: Carry_out
  TriState_Switch tristate_switch_1 (
    .Y0(Y0), .Y1(Y1), .Y2(Y2), .Y3(Y3), .Y4(Y4), .Y5(Y5), .Y6(Y6), .Y7(Y7), .I0(flipflop_8bit_1_y0),
    .I1(flipflop_8bit_1_y1), .I2(flipflop_8bit_1_y2), .I3(flipflop_8bit_1_y3), .I4(flipflop_8bit_1_y4),
    .I5(flipflop_8bit_1_y5), .I6(flipflop_8bit_1_y6), .I7(flipflop_8bit_1_y7), .Enable(PC_OUT));
  and and_2 (and_2_out, not_2_out, Din0);
  and and_3 (and_3_out, not_2_out, Din1);
  and and_4 (and_4_out, not_2_out, Din2);
  and and_5 (and_5_out, not_2_out, Din3);
  and and_6 (and_6_out, not_2_out, Din4);
  or or_2 (or_2_out, flipflop_8bit_1_y4, flipflop_8bit_1_y5, flipflop_8bit_1_y6, flipflop_8bit_1_y7);
  and and_7 (and_7_out, not_2_out, Din5);
  and and_8 (and_8_out, not_2_out, Din6);
  nor nor_1 (Zero, or_3_out, or_2_out);
  and and_9 (and_9_out, not_2_out, Din7);
  or or_3 (or_3_out, flipflop_8bit_1_y0, flipflop_8bit_1_y1, flipflop_8bit_1_y2, flipflop_8bit_1_y3);
  Multiplexor_2_8bits multiplexor_2_8bits_1 (
    .A0(full_adder_1_y), .B0(and_2_out), .A1(full_adder_2_y), .B1(and_3_out), .A2(full_adder_3_y),
    .B2(and_4_out), .A3(full_adder_4_y), .B3(and_5_out), .A4(full_adder_5_y), .B4(and_6_out),
    .A5(full_adder_6_y), .B5(and_7_out), .A6(full_adder_7_y), .B6(and_8_out), .A7(full_adder_8_y),
    .B7(and_9_out), .Y0(multiplexor_2_8bits_1_y0), .Y1(multiplexor_2_8bits_1_y1),
    .Y2(multiplexor_2_8bits_1_y2), .Y3(multiplexor_2_8bits_1_y3), .Y4(multiplexor_2_8bits_1_y4),
    .Y5(multiplexor_2_8bits_1_y5), .Y6(multiplexor_2_8bits_1_y6), .Y7(multiplexor_2_8bits_1_y7), .S0(or_1_out));
  Flipflop_8bit flipflop_8bit_1 (
    .Y0(flipflop_8bit_1_y0), .Y1(flipflop_8bit_1_y1), .Y2(flipflop_8bit_1_y2), .Y3(flipflop_8bit_1_y3),
    .Y4(flipflop_8bit_1_y4), .Y5(flipflop_8bit_1_y5), .Y6(flipflop_8bit_1_y6), .Y7(flipflop_8bit_1_y7),
    .CLK(CLK), .EN(1'b1), .D0(multiplexor_2_8bits_1_y0), .D1(multiplexor_2_8bits_1_y1),
    .D2(multiplexor_2_8bits_1_y2), .D3(multiplexor_2_8bits_1_y3), .D4(multiplexor_2_8bits_1_y4),
    .D5(multiplexor_2_8bits_1_y5), .D6(multiplexor_2_8bits_1_y6), .D7(multiplexor_2_8bits_1_y7));
endmodule
