// Digital circuit RAM.dig as structural Verilog
module RAM (
  input  CLK,
  input  R_W,
  input  S0,
  input  S1,
  input  I0,
  input  I1,
  input  I2,
  input  I3,
  input  I4,
  input  I5,
  input  I6,
  input  I7,
  output RAM10,
  output RAM11,
  output RAM12,
  output RAM13,
  output RAM14,
  output RAM15,
  output RAM16,
  output RAM17,
  output RAM26,
  output RAM27,
  output RAM20,
  output RAM21,
  output RAM22,
  output RAM23,
  output RAM24,
  output RAM25,
  output RAM34,
  output RAM35,
  output RAM36,
  output RAM37,
  output RAM30,
  output RAM31,
  output RAM32,
  output RAM33,
  output RAM46,
  output RAM47,
  output RAM40,
  output RAM41,
  output RAM42,
  output RAM43,
  output RAM44,
  output RAM45,
  output Y0,
  output Y1,
  output Y2,
  output Y3,
  output Y4,
  output Y5,
  output Y6,
  output Y7
);

  wire demultiplexor_1_y0, demultiplexor_1_y1, demultiplexor_1_y2, demultiplexor_1_y3, multiplexor_4_1_y,
       multiplexor_4_2_y, multiplexor_4_3_y, multiplexor_4_4_y, multiplexor_4_5_y, multiplexor_4_6_y,
       multiplexor_4_7_y, multiplexor_4_8_y, not_1_out;

  Demultiplexor demultiplexor_1 (
    .S0(S0), .S1(S1), .I(R_W), .Y0(demultiplexor_1_y0), .Y1(demultiplexor_1_y1), .Y2(demultiplexor_1_y2),
    .Y3(demultiplexor_1_y3));
  Flipflop_8bit flipflop_8bit_1 (
    .Y0(RAM10), .Y1(RAM11), .Y2(RAM12), .Y3(RAM13), .Y4(RAM14), .Y5(RAM15), .Y6(RAM16), .Y7(RAM17),
    .CLK(CLK), .EN(demultiplexor_1_y0), .D0(I0), .D1(I1), .D2(I2), .D3(I3), .D4(I4), .D5(I5), .D6(I6), .D7(I7));
  Flipflop_8bit flipflop_8bit_2 (
    .Y0(RAM20), .Y1(RAM21), .Y2(RAM22), .Y3(RAM23), .Y4(RAM24), .Y5(RAM25), .Y6(RAM26), .Y7(RAM27),
    .CLK(CLK), .EN(demultiplexor_1_y1), .D0(I0), .D1(I1), .D2(I2), .D3(I3), .D4(I4), .D5(I5), .D6(I6), .D7(I7));
  Flipflop_8bit flipflop_8bit_3 (
    .Y0(RAM30), .Y1(RAM31), .Y2(RAM32), .Y3(RAM33), .Y4(RAM34), .Y5(RAM25), .Y6(RAM36), .Y7(RAM37),
    .CLK(CLK), .EN(demultiplexor_1_y2), .D0(I0), .D1(I1), .D2(I2), .D3(I3), .D4(I4), .D5(I5), .D6(I6), .D7(I7));
  Flipflop_8bit flipflop_8bit_4 (
    .Y0(RAM40), .Y1(RAM41), .Y2(RAM42), .Y3(RAM43), .Y4(RAM44), .Y5(RAM45), .Y6(RAM46), .Y7(RAM47),
    .CLK(CLK), .EN(demultiplexor_1_y3), .D0(I0), .D1(I1), .D2(I2), .D3(I3), .D4(I4), .D5(I5), .D6(I6), .D7(I7));
  Multiplexor_4 multiplexor_4_1 (
    .Y(multiplexor_4_1_y), .I0(RAM10), .I1(RAM20), .I2(RAM30), .I3(RAM40), .S0(S0), .S1(S1));
  not not_1 (not_1_out, R_W);
  Multiplexor_4 multiplexor_4_2 (
    .Y(multiplexor_4_2_y), .I0(RAM11), .I1(RAM21), .I2(RAM31), .I3(RAM41), .S0(S0), .S1(S1));
  Multiplexor_4 multiplexor_4_3 (
    .Y(multiplexor_4_3_y), .I0(RAM12), .I1(RAM22), .I2(RAM32), .I3(RAM42), .S0(S0), .S1(S1));
  Flipflop_8bit flipflop_8bit_5 (
    .Y0(Y0), .Y1(Y1), .Y2(Y2), .Y3(Y3), .Y4(Y4), .Y5(Y5), .Y6(Y6), .Y7(Y7), .CLK(CLK), .EN(not_1_out),
    .D0(multiplexor_4_1_y), .D1(multiplexor_4_2_y), .D2(multiplexor_4_3_y), .D3(multiplexor_4_4_y),
    .D4(multiplexor_4_5_y), .D5(multiplexor_4_6_y), .D6(multiplexor_4_7_y), .D7(multiplexor_4_8_y));
  Multiplexor_4 multiplexor_4_4 (
    .Y(multiplexor_4_4_y), .I0(RAM13), .I1(RAM23), .I2(RAM33), .I3(RAM43), .S0(S0), .S1(S1));
  Multiplexor_4 multiplexor_4_5 (
    .Y(multiplexor_4_5_y), .I0(RAM14), .I1(RAM24), .I2(RAM34), .I3(RAM44), .S0(S0), .S1(S1));
  Multiplexor_4 multiplexor_4_6 (
    .Y(multiplexor_4_6_y), .I0(RAM15), .I1(RAM25), .I2(RAM25), .I3(RAM45), .S0(S0), .S1(S1));
  Multiplexor_4 multiplexor_4_7 (
    .Y(multiplexor_4_7_y), .I0(RAM16), .I1(RAM26), .I2(RAM36), .I3(RAM46), .S0(S0), .S1(S1));
  Multiplexor_4 multiplexor_4_8 (
    .Y(multiplexor_4_8_y), .I0(RAM17), .I1(RAM27), .I2(RAM37), .I3(RAM47), .S0(S0), .S1(S1));

  assign RAM35 = RAM25;
endmodule
