// Digital circuit RAM64B.dig as structural Verilog
module RAM64B (
  input  D0,
  input  D1,
  input  D2,
  input  D3,
  input  D4,
  input  D5,
  input  D6,
  input  D7,
  input  RAM_IN,
  input  RAM_OUT,
  input  CLK,
  input  S1,
  input  S2,
  input  S3,
  input  S4,
  input  S5,
  input  S0,
  output Y0,
  output Y1,
  output Y2,
  output Y3,
  output Y4,
  output Y5,
  output Y6,
  output Y7
);

  wire demultiplexor_1_y0, demultiplexor_1_y1, demultiplexor_1_y2, demultiplexor_1_y3, demultiplexor_2_y0,
       demultiplexor_2_y1, demultiplexor_2_y2, demultiplexor_2_y3, demultiplexor_3_y0, demultiplexor_3_y1,
       demultiplexor_3_y2, demultiplexor_3_y3, demultiplexor_4_y0, demultiplexor_4_y1, demultiplexor_4_y2,
       demultiplexor_4_y3, demultiplexor_5_y0, demultiplexor_5_y1, demultiplexor_5_y2, demultiplexor_5_y3,
       demultiplexor_6_y0, demultiplexor_6_y1, demultiplexor_6_y2, demultiplexor_6_y3, demultiplexor_7_y0,
       demultiplexor_7_y1, demultiplexor_7_y2, demultiplexor_7_y3, demultiplexor_8_y0, demultiplexor_8_y1,
       demultiplexor_8_y2, demultiplexor_8_y3, demultiplexor_9_y0, demultiplexor_9_y1, demultiplexor_9_y2,
       demultiplexor_9_y3, demultiplexor_10_y0, demultiplexor_10_y1, demultiplexor_10_y2,
       demultiplexor_10_y3, multiplexor_4_1_y, multiplexor_4_2_y, multiplexor_4_3_y, multiplexor_4_4_y,
       multiplexor_4_5_y, multiplexor_4_6_y, multiplexor_4_7_y, multiplexor_4_8_y, ram_16b_1_y0,
       ram_16b_1_y1, ram_16b_1_y2, ram_16b_1_y3, ram_16b_1_y4, ram_16b_1_y5, ram_16b_1_y6, ram_16b_1_y7,
       ram_16b_2_y0, ram_16b_2_y1, ram_16b_2_y2, ram_16b_2_y3, ram_16b_2_y4, ram_16b_2_y5, ram_16b_2_y6,
       ram_16b_2_y7, ram_16b_3_y0, ram_16b_3_y1, ram_16b_3_y2, ram_16b_3_y3, ram_16b_3_y4, ram_16b_3_y5,
       ram_16b_3_y6, ram_16b_3_y7, ram_16b_4_y0, ram_16b_4_y1, ram_16b_4_y2, ram_16b_4_y3, ram_16b_4_y4,
       ram_16b_4_y5, ram_16b_4_y6, ram_16b_4_y7;

  Demultiplexor demultiplexor_1 (
    .S0(S4), .S1(S5), .I(D0), .Y0(demultiplexor_1_y0), .Y1(demultiplexor_1_y1), .Y2(demultiplexor_1_y2),
    .Y3(demultiplexor_1_y3));
  Demultiplexor demultiplexor_2 (
    .S0(S4), .S1(S5), .I(D1), .Y0(demultiplexor_2_y0), .Y1(demultiplexor_2_y1), .Y2(demultiplexor_2_y2),
    .Y3(demultiplexor_2_y3));
  Demultiplexor demultiplexor_3 (
    .S0(S4), .S1(S5), .I(D2), .Y0(demultiplexor_3_y0), .Y1(demultiplexor_3_y1), .Y2(demultiplexor_3_y2),
    .Y3(demultiplexor_3_y3));
  Demultiplexor demultiplexor_4 (
    .S0(S4), .S1(S5), .I(D3), .Y0(demultiplexor_4_y0), .Y1(demultiplexor_4_y1), .Y2(demultiplexor_4_y2),
    .Y3(demultiplexor_4_y3));
  Demultiplexor demultiplexor_5 (
    .S0(S4), .S1(S5), .I(D4), .Y0(demultiplexor_5_y0), .Y1(demultiplexor_5_y1), .Y2(demultiplexor_5_y2),
    .Y3(demultiplexor_5_y3));
  Demultiplexor demultiplexor_6 (
    .S0(S4), .S1(S5), .I(D5), .Y0(demultiplexor_6_y0), .Y1(demultiplexor_6_y1), .Y2(demultiplexor_6_y2),
    .Y3(demultiplexor_6_y3));
  Demultiplexor demultiplexor_7 (
    .S0(S4), .S1(S5), .I(D6), .Y0(demultiplexor_7_y0), .Y1(demultiplexor_7_y1), .Y2(demultiplexor_7_y2),
    .Y3(demultiplexor_7_y3));
  Demultiplexor demultiplexor_8 (
    .S0(S4), .S1(S5), .I(D7), .Y0(demultiplexor_8_y0), .Y1(demultiplexor_8_y1), .Y2(demultiplexor_8_y2),
    .Y3(demultiplexor_8_y3));
  Demultiplexor demultiplexor_9 (
    .S0(S4), .S1(S5), .I(RAM_IN), .Y0(demultiplexor_9_y0), .Y1(demultiplexor_9_y1), .Y2(demultiplexor_9_y2),
    .Y3(demultiplexor_9_y3));
  Demultiplexor demultiplexor_10 (
    .S0(S4), .S1(S5), .I(RAM_OUT), .Y0(demultiplexor_10_y0), .Y1(demultiplexor_10_y1),
    .Y2(demultiplexor_10_y2), .Y3(demultiplexor_10_y3));
  RAM_16B ram_16b_1 (
    .Y0(ram_16b_1_y0), .Y1(ram_16b_1_y1), .Y2(ram_16b_1_y2), .Y3(ram_16b_1_y3), .Y4(ram_16b_1_y4),
    .Y5(ram_16b_1_y5), .Y6(ram_16b_1_y6), .Y7(ram_16b_1_y7), .RAM_IN(demultiplexor_9_y0),
    .RAM_OUT(demultiplexor_10_y0), .CLK(CLK), .S0(S0), .S1(S1), .S2(S2), .S3(S3), .D0(demultiplexor_1_y0),
    .D1(demultiplexor_2_y0), .D2(demultiplexor_3_y0), .D3(demultiplexor_4_y0), .D4(demultiplexor_5_y0),
    .D5(demultiplexor_6_y0), .D6(demultiplexor_7_y0), .D7(demultiplexor_8_y0));
  RAM_16B ram_16b_2 (
    .Y0(ram_16b_2_y0), .Y1(ram_16b_2_y1), .Y2(ram_16b_2_y2), .Y3(ram_16b_2_y3), .Y4(ram_16b_2_y4),
    .Y5(ram_16b_2_y5), .Y6(ram_16b_2_y6), .Y7(ram_16b_2_y7), .RAM_IN(demultiplexor_9_y1),
    .RAM_OUT(demultiplexor_10_y1), .CLK(CLK), .S0(S0), .S1(S1), .S2(S2), .S3(S3), .D0(demultiplexor_1_y1),
    .D1(demultiplexor_2_y1), .D2(demultiplexor_3_y1), .D3(demultiplexor_4_y1), .D4(demultiplexor_5_y1),
    .D5(demultiplexor_6_y1), .D6(demultiplexor_7_y1), .D7(demultiplexor_8_y1));
  RAM_16B ram_16b_3 (
    .Y0(ram_16b_3_y0), .Y1(ram_16b_3_y1), .Y2(ram_16b_3_y2), .Y3(ram_16b_3_y3), .Y4(ram_16b_3_y4),
    .Y5(ram_16b_3_y5), .Y6(ram_16b_3_y6), .Y7(ram_16b_3_y7), .RAM_IN(demultiplexor_9_y2),
    .RAM_OUT(demultiplexor_10_y2), .CLK(CLK), .S0(S0), .S1(S1), .S2(S2), .S3(S3), .D0(demultiplexor_1_y2),
    .D1(demultiplexor_2_y2), .D2(demultiplexor_3_y2), .D3(demultiplexor_4_y2), .D4(demultiplexor_5_y2),
    .D5(demultiplexor_6_y2), .D6(demultiplexor_7_y2), .D7(demultiplexor_8_y2));
  RAM_16B ram_16b_4 (
    .Y0(ram_16b_4_y0), .Y1(ram_16b_4_y1), .Y2(ram_16b_4_y2), .Y3(ram_16b_4_y3), .Y4(ram_16b_4_y4),
    .Y5(ram_16b_4_y5), .Y6(ram_16b_4_y6), .Y7(ram_16b_4_y7), .RAM_IN(demultiplexor_9_y3),
    .RAM_OUT(demultiplexor_10_y3), .CLK(CLK), .S0(S0), .S1(S1), .S2(S2), .S3(S3), .D0(demultiplexor_1_y3),
    .D1(demultiplexor_2_y3), .D2(demultiplexor_3_y3), .D3(demultiplexor_4_y3), .D4(demultiplexor_5_y3),
    .D5(demultiplexor_6_y3), .D6(demultiplexor_7_y3), .D7(demultiplexor_8_y3));
  Multiplexor_4 multiplexor_4_1 (
    .Y(multiplexor_4_1_y), .I0(ram_16b_1_y0), .I1(ram_16b_2_y0), .I2(ram_16b_3_y0), .I3(ram_16b_4_y0),
    .S0(S4), .S1(S5));
  Multiplexor_4 multiplexor_4_2 (
    .Y(multiplexor_4_2_y), .I0(ram_16b_1_y1), .I1(ram_16b_2_y1), .I2(ram_16b_3_y1), .I3(ram_16b_4_y1),
    .S0(S4), .S1(S5));
  Multiplexor_4 multiplexor_4_3 (
    .Y(multiplexor_4_3_y), .I0(ram_16b_1_y2), .I1(ram_16b_2_y2), .I2(ram_16b_3_y2), .I3(ram_16b_4_y2),
    .S0(S4), .S1(S5));
  Multiplexor_4 multiplexor_4_4 (
    .Y(multiplexor_4_4_y), .I0(ram_16b_1_y3), .I1(ram_16b_2_y3), .I2(ram_16b_3_y3), .I3(ram_16b_4_y3),
    .S0(S4), .S1(S5));
  Multiplexor_4 multiplexor_4_5 (
    .Y(multiplexor_4_5_y), .I0(ram_16b_1_y4), .I1(ram_16b_2_y4), .I2(ram_16b_3_y4), .I3(ram_16b_4_y4),
    .S0(S4), .S1(S5));
  Multiplexor_4 multiplexor_4_6 (
    .Y(multiplexor_4_6_y), .I0(ram_16b_1_y5), .I1(ram_16b_2_y5), .I2(ram_16b_3_y5), .I3(ram_16b_4_y5),
    .S0(S4), .S1(S5));
  Multiplexor_4 multiplexor_4_7 (
    .Y(multiplexor_4_7_y), .I0(ram_16b_1_y6), .I1(ram_16b_2_y6), .I2(ram_16b_3_y6), .I3(ram_16b_4_y6),
    .S0(S4), .S1(S5));
  Multiplexor_4 multiplexor_4_8 (
    .Y(multiplexor_4_8_y), .I0(ram_16b_1_y7), .I1(ram_16b_2_y7), .I2(ram_16b_3_y7), .I3(ram_16b_4_y7),
    .S0(S4), .S1(S5));
  TriState_Switch tristate_switch_1 (
    .Y0(Y0), .Y1(Y1), .Y2(Y2), .Y3(Y3), .Y4(Y4), .Y5(Y5), .Y6(Y6), .Y7(Y7), .I0(multiplexor_4_1_y),
    .I1(multiplexor_4_2_y), .I2(multiplexor_4_3_y), .I3(multiplexor_4_4_y), .I4(multiplexor_4_5_y),
    .I5(multiplexor_4_6_y), .I6(multiplexor_4_7_y), .I7(multiplexor_4_8_y), .Enable(RAM_OUT));
endmodule
