// Digital circuit RAM_16B.dig as structural Verilog
module RAM_16B (
  input  S0,
  input  S1,
  input  S2,
  input  S3,
  input  D0,
  input  RAM_IN,
  input  RAM_OUT,
  input  CLK,
  input  D1,
  input  D2,
  input  D3,
  input  D4,
  input  D5,
  input  D6,
  input  D7,
  output Y0,
  output Y1,
  output Y2,
  output Y3,
  output Y4,
  output Y5,
  output Y6,
  output Y7
);

  wire d_flipflop_raisingedge_1_y, d_flipflop_raisingedge_2_y, demultiplexor_1_y0, demultiplexor_1_y1,
       demultiplexor_1_y2, demultiplexor_1_y3, demultiplexor_2_y0, demultiplexor_2_y1, demultiplexor_2_y2,
       demultiplexor_2_y3, demultiplexor_3_y0, demultiplexor_3_y1, demultiplexor_3_y2, demultiplexor_3_y3,
       demultiplexor_4_y0, demultiplexor_4_y1, demultiplexor_4_y2, demultiplexor_4_y3, demultiplexor_5_y0,
       demultiplexor_5_y1, demultiplexor_5_y2, demultiplexor_5_y3, demultiplexor_6_y0, demultiplexor_6_y1,
       demultiplexor_6_y2, demultiplexor_6_y3, demultiplexor_7_y0, demultiplexor_7_y1, demultiplexor_7_y2,
       demultiplexor_7_y3, demultiplexor_8_y0, demultiplexor_8_y1, demultiplexor_8_y2, demultiplexor_8_y3,
       demultiplexor_9_y0, demultiplexor_9_y1, demultiplexor_9_y2, demultiplexor_9_y3, demultiplexor_10_y0,
       demultiplexor_10_y1, demultiplexor_10_y2, demultiplexor_10_y3, ram_4bytes_1_p14, ram_4bytes_1_p15,
       ram_4bytes_1_p16, ram_4bytes_1_p17, ram_4bytes_1_p18, ram_4bytes_1_p19, ram_4bytes_1_p20,
       ram_4bytes_1_p21, ram_4bytes_2_p14, ram_4bytes_2_p15, ram_4bytes_2_p16, ram_4bytes_2_p17,
       ram_4bytes_2_p18, ram_4bytes_2_p19, ram_4bytes_2_p20, ram_4bytes_2_p21, ram_4bytes_3_p14,
       ram_4bytes_3_p15, ram_4bytes_3_p16, ram_4bytes_3_p17, ram_4bytes_3_p18, ram_4bytes_3_p19,
       ram_4bytes_3_p20, ram_4bytes_3_p21, ram_4bytes_4_p14, ram_4bytes_4_p15, ram_4bytes_4_p16,
       ram_4bytes_4_p17, ram_4bytes_4_p18, ram_4bytes_4_p19, ram_4bytes_4_p20, ram_4bytes_4_p21;

  Demultiplexor demultiplexor_1 (
    .S0(S2), .S1(S3), .I(D0), .Y0(demultiplexor_1_y0), .Y1(demultiplexor_1_y1), .Y2(demultiplexor_1_y2),
    .Y3(demultiplexor_1_y3));
  Demultiplexor demultiplexor_2 (
    .S0(S2), .S1(S3), .I(D1), .Y0(demultiplexor_2_y0), .Y1(demultiplexor_2_y1), .Y2(demultiplexor_2_y2),
    .Y3(demultiplexor_2_y3));
  Demultiplexor demultiplexor_3 (
    .S0(S2), .S1(S3), .I(D2), .Y0(demultiplexor_3_y0), .Y1(demultiplexor_3_y1), .Y2(demultiplexor_3_y2),
    .Y3(demultiplexor_3_y3));
  Demultiplexor demultiplexor_4 (
    .S0(S2), .S1(S3), .I(D3), .Y0(demultiplexor_4_y0), .Y1(demultiplexor_4_y1), .Y2(demultiplexor_4_y2),
    .Y3(demultiplexor_4_y3));
  Demultiplexor demultiplexor_5 (
    .S0(S2), .S1(S3), .I(D4), .Y0(demultiplexor_5_y0), .Y1(demultiplexor_5_y1), .Y2(demultiplexor_5_y2),
    .Y3(demultiplexor_5_y3));
  Demultiplexor demultiplexor_6 (
    .S0(S2), .S1(S3), .I(D5), .Y0(demultiplexor_6_y0), .Y1(demultiplexor_6_y1), .Y2(demultiplexor_6_y2),
    .Y3(demultiplexor_6_y3));
  Demultiplexor demultiplexor_7 (
    .S0(S2), .S1(S3), .I(D6), .Y0(demultiplexor_7_y0), .Y1(demultiplexor_7_y1), .Y2(demultiplexor_7_y2),
    .Y3(demultiplexor_7_y3));
  Demultiplexor demultiplexor_8 (
    .S0(S2), .S1(S3), .I(D7), .Y0(demultiplexor_8_y0), .Y1(demultiplexor_8_y1), .Y2(demultiplexor_8_y2),
    .Y3(demultiplexor_8_y3));
  Demultiplexor demultiplexor_9 (
    .S0(S2), .S1(S3), .I(RAM_IN), .Y0(demultiplexor_9_y0), .Y1(demultiplexor_9_y1), .Y2(demultiplexor_9_y2),
    .Y3(demultiplexor_9_y3));
  Demultiplexor demultiplexor_10 (
    .S0(S2), .S1(S3), .I(RAM_OUT), .Y0(demultiplexor_10_y0), .Y1(demultiplexor_10_y1),
    .Y2(demultiplexor_10_y2), .Y3(demultiplexor_10_y3));
  // RAM_4bytes ram_4bytes_1: pin names not known; wires that end beside it: demultiplexor_1_y0, demultiplexor_2_y0, demultiplexor_3_y0, demultiplexor_4_y0, demultiplexor_5_y0, demultiplexor_6_y0, demultiplexor_7_y0, demultiplexor_8_y0, S0, S1, demultiplexor_10_y0, demultiplexor_9_y0, CLK, ram_4bytes_1_p14, ram_4bytes_1_p15, ram_4bytes_1_p16, ram_4bytes_1_p17, ram_4bytes_1_p18, ram_4bytes_1_p19, ram_4bytes_1_p20, ram_4bytes_1_p21
  // RAM_4bytes ram_4bytes_2: pin names not known; wires that end beside it: demultiplexor_1_y1, demultiplexor_2_y1, demultiplexor_3_y1, demultiplexor_4_y1, demultiplexor_5_y1, demultiplexor_6_y1, demultiplexor_7_y1, demultiplexor_8_y1, S0, S1, demultiplexor_10_y1, demultiplexor_9_y1, CLK, ram_4bytes_2_p14, ram_4bytes_2_p15, ram_4bytes_2_p16, ram_4bytes_2_p17, ram_4bytes_2_p18, ram_4bytes_2_p19, ram_4bytes_2_p20, ram_4bytes_2_p21
  // RAM_4bytes ram_4bytes_3: pin names not known; wires that end beside it: demultiplexor_1_y2, demultiplexor_2_y2, demultiplexor_3_y2, demultiplexor_4_y2, demultiplexor_5_y2, demultiplexor_6_y2, demultiplexor_7_y2, demultiplexor_8_y2, S0, S1, demultiplexor_10_y2, demultiplexor_9_y2, CLK, ram_4bytes_3_p14, ram_4bytes_3_p15, ram_4bytes_3_p16, ram_4bytes_3_p17, ram_4bytes_3_p18, ram_4bytes_3_p19, ram_4bytes_3_p20, ram_4bytes_3_p21
  // RAM_4bytes ram_4bytes_4: pin names not known; wires that end beside it: demultiplexor_1_y3, demultiplexor_2_y3, demultiplexor_3_y3, demultiplexor_4_y3, demultiplexor_5_y3, demultiplexor_6_y3, demultiplexor_7_y3, demultiplexor_8_y3, S0, S1, demultiplexor_10_y3, demultiplexor_9_y3, CLK, ram_4bytes_4_p14, ram_4bytes_4_p15, ram_4bytes_4_p16, ram_4bytes_4_p17, ram_4bytes_4_p18, ram_4bytes_4_p19, ram_4bytes_4_p20, ram_4bytes_4_p21
  D_FlipFlop_RaisingEdge d_flipflop_raisingedge_1 (.D(S2), .CLK(CLK), .Y(d_flipflop_raisingedge_1_y));
  D_FlipFlop_RaisingEdge d_flipflop_raisingedge_2 (.D(S3), .CLK(CLK), .Y(d_flipflop_raisingedge_2_y));
  Multiplexor_4 multiplexor_4_1 (
    .Y(Y0), .I0(ram_4bytes_1_p14), .I1(ram_4bytes_2_p14), .I2(ram_4bytes_3_p14), .I3(ram_4bytes_4_p14),
    .S0(d_flipflop_raisingedge_1_y), .S1(d_flipflop_raisingedge_2_y));
  Multiplexor_4 multiplexor_4_2 (
    .Y(Y1), .I0(ram_4bytes_1_p15), .I1(ram_4bytes_2_p15), .I2(ram_4bytes_3_p15), .I3(ram_4bytes_4_p15),
    .S0(d_flipflop_raisingedge_1_y), .S1(d_flipflop_raisingedge_2_y));
  Multiplexor_4 multiplexor_4_3 (
    .Y(Y2), .I0(ram_4bytes_1_p16), .I1(ram_4bytes_2_p16), .I2(ram_4bytes_3_p16), .I3(ram_4bytes_4_p16),
    .S0(d_flipflop_raisingedge_1_y), .S1(d_flipflop_raisingedge_2_y));
  Multiplexor_4 multiplexor_4_4 (
    .Y(Y3), .I0(ram_4bytes_1_p17), .I1(ram_4bytes_2_p17), .I2(ram_4bytes_3_p17), .I3(ram_4bytes_4_p17),
    .S0(d_flipflop_raisingedge_1_y), .S1(d_flipflop_raisingedge_2_y));
  Multiplexor_4 multiplexor_4_5 (
    .Y(Y4), .I0(ram_4bytes_1_p18), .I1(ram_4bytes_2_p18), .I2(ram_4bytes_3_p18), .I3(ram_4bytes_4_p18),
    .S0(d_flipflop_raisingedge_1_y), .S1(d_flipflop_raisingedge_2_y));
  Multiplexor_4 multiplexor_4_6 (
    .Y(Y5), .I0(ram_4bytes_1_p19), .I1(ram_4bytes_2_p19), .I2(ram_4bytes_3_p19), .I3(ram_4bytes_4_p19),
    .S0(d_flipflop_raisingedge_1_y), .S1(d_flipflop_raisingedge_2_y));
  Multiplexor_4 multiplexor_4_7 (
    .Y(Y6), .I0(ram_4bytes_1_p20), .I1(ram_4bytes_2_p20), .I2(ram_4bytes_3_p20), .I3(ram_4bytes_4_p20),
    .S0(d_flipflop_raisingedge_1_y), .S1(d_flipflop_raisingedge_2_y));
  Multiplexor_4 multiplexor_4_8 (
    .Y(Y7), .I0(ram_4bytes_1_p21), .I1(ram_4bytes_2_p21), .I2(ram_4bytes_3_p21), .I3(ram_4bytes_4_p21),
    .S0(d_flipflop_raisingedge_1_y), .S1(d_flipflop_raisingedge_2_y));
endmodule
