// Digital circuit RAM_4B.dig as structural Verilog
module RAM_4B (
  input  D0,
  input  D1,
  input  D2,
  input  D3,
  input  D4,
  input  D5,
  input  D6,
  input  D7,
  input  S0,
  input  S1,
  input  RAM_OUT,
  input  RAM_IN,
  input  CLK,
  output Y0,
  output Y1,
  output Y2,
  output Y3,
  output Y4,
  output Y5,
  output Y6,
  output Y7
);

  wire demultiplexor_1_y0, demultiplexor_1_y1, demultiplexor_1_y2, demultiplexor_1_y3, flipflop_8bit_1_y0,
       flipflop_8bit_1_y1, flipflop_8bit_1_y2, flipflop_8bit_1_y3, flipflop_8bit_1_y4, flipflop_8bit_1_y5,
       flipflop_8bit_1_y6, flipflop_8bit_1_y7, flipflop_8bit_2_y0, flipflop_8bit_2_y1, flipflop_8bit_2_y2,
       flipflop_8bit_2_y3, flipflop_8bit_2_y4, flipflop_8bit_2_y5, flipflop_8bit_2_y6, flipflop_8bit_2_y7,
       flipflop_8bit_3_y0, flipflop_8bit_3_y1, flipflop_8bit_3_y2, flipflop_8bit_3_y3, flipflop_8bit_3_y4,
       flipflop_8bit_3_y5, flipflop_8bit_3_y6, flipflop_8bit_3_y7, flipflop_8bit_4_y0, flipflop_8bit_4_y1,
       flipflop_8bit_4_y2, flipflop_8bit_4_y3, flipflop_8bit_4_y4, flipflop_8bit_4_y5, flipflop_8bit_4_y6,
       flipflop_8bit_4_y7, multiplexor_4_1_y, multiplexor_4_2_y, multiplexor_4_3_y, multiplexor_4_4_y,
       multiplexor_4_5_y, multiplexor_4_6_y, multiplexor_4_7_y, multiplexor_4_8_y;

  Demultiplexor demultiplexor_1 (
    .S0(S0), .S1(S1), .I(RAM_IN), .Y0(demultiplexor_1_y0), .Y1(demultiplexor_1_y1), .Y2(demultiplexor_1_y2),
    .Y3(demultiplexor_1_y3));
  Flipflop_8bit flipflop_8bit_1 (
    .Y0(flipflop_8bit_1_y0), .Y1(flipflop_8bit_1_y1), .Y2(flipflop_8bit_1_y2), .Y3(flipflop_8bit_1_y3),
    .Y4(flipflop_8bit_1_y4), .Y5(flipflop_8bit_1_y5), .Y6(flipflop_8bit_1_y6), .Y7(flipflop_8bit_1_y7),
    .CLK(CLK), .EN(demultiplexor_1_y0), .D0(D0), .D1(D1), .D2(D2), .D3(D3), .D4(D4), .D5(D5), .D6(D6), .D7(D7));
  Flipflop_8bit flipflop_8bit_2 (
    .Y0(flipflop_8bit_2_y0), .Y1(flipflop_8bit_2_y1), .Y2(flipflop_8bit_2_y2), .Y3(flipflop_8bit_2_y3),
    .Y4(flipflop_8bit_2_y4), .Y5(flipflop_8bit_2_y5), .Y6(flipflop_8bit_2_y6), .Y7(flipflop_8bit_2_y7),
    .CLK(CLK), .EN(demultiplexor_1_y1), .D0(D0), .D1(D1), .D2(D2), .D3(D3), .D4(D4), .D5(D5), .D6(D6), .D7(D7));
  Flipflop_8bit flipflop_8bit_3 (
    .Y0(flipflop_8bit_3_y0), .Y1(flipflop_8bit_3_y1), .Y2(flipflop_8bit_3_y2), .Y3(flipflop_8bit_3_y3),
    .Y4(flipflop_8bit_3_y4), .Y5(flipflop_8bit_3_y5), .Y6(flipflop_8bit_3_y6), .Y7(flipflop_8bit_3_y7),
    .CLK(CLK), .EN(demultiplexor_1_y2), .D0(D0), .D1(D1), .D2(D2), .D3(D3), .D4(D4), .D5(D5), .D6(D6), .D7(D7));
  Flipflop_8bit flipflop_8bit_4 (
    .Y0(flipflop_8bit_4_y0), .Y1(flipflop_8bit_4_y1), .Y2(flipflop_8bit_4_y2), .Y3(flipflop_8bit_4_y3),
    .Y4(flipflop_8bit_4_y4), .Y5(flipflop_8bit_4_y5), .Y6(flipflop_8bit_4_y6), .Y7(flipflop_8bit_4_y7),
    .CLK(CLK), .EN(demultiplexor_1_y3), .D0(D0), .D1(D1), .D2(D2), .D3(D3), .D4(D4), .D5(D5), .D6(D6), .D7(D7));
  Multiplexor_4 multiplexor_4_1 (
    .Y(multiplexor_4_1_y), .I0(flipflop_8bit_1_y0), .I1(flipflop_8bit_2_y0), .I2(flipflop_8bit_3_y0),
    .I3(flipflop_8bit_4_y0), .S0(S0), .S1(S1));
  Multiplexor_4 multiplexor_4_2 (
    .Y(multiplexor_4_2_y), .I0(flipflop_8bit_1_y1), .I1(flipflop_8bit_2_y1), .I2(flipflop_8bit_3_y1),
    .I3(flipflop_8bit_4_y1), .S0(S0), .S1(S1));
  Multiplexor_4 multiplexor_4_3 (
    .Y(multiplexor_4_3_y), .I0(flipflop_8bit_1_y2), .I1(flipflop_8bit_2_y2), .I2(flipflop_8bit_3_y2),
    .I3(flipflop_8bit_4_y2), .S0(S0), .S1(S1));
  Flipflop_8bit flipflop_8bit_5 (
    .Y0(Y0), .Y1(Y1), .Y2(Y2), .Y3(Y3), .Y4(Y4), .Y5(Y5), .Y6(Y6), .Y7(Y7), .CLK(CLK), .EN(RAM_OUT),
    .D0(multiplexor_4_1_y), .D1(multiplexor_4_2_y), .D2(multiplexor_4_3_y), .D3(multiplexor_4_4_y),
    .D4(multiplexor_4_5_y), .D5(multiplexor_4_6_y), .D6(multiplexor_4_7_y), .D7(multiplexor_4_8_y));
  Multiplexor_4 multiplexor_4_4 (
    .Y(multiplexor_4_4_y), .I0(flipflop_8bit_1_y3), .I1(flipflop_8bit_2_y3), .I2(flipflop_8bit_3_y3),
    .I3(flipflop_8bit_4_y3), .S0(S0), .S1(S1));
  Multiplexor_4 multiplexor_4_5 (
    .Y(multiplexor_4_5_y), .I0(flipflop_8bit_1_y4), .I1(flipflop_8bit_2_y4), .I2(flipflop_8bit_3_y4),
    .I3(flipflop_8bit_4_y4), .S0(S0), .S1(S1));
  Multiplexor_4 multiplexor_4_6 (
    .Y(multiplexor_4_6_y), .I0(flipflop_8bit_1_y5), .I1(flipflop_8bit_2_y5), .I2(flipflop_8bit_3_y5),
    .I3(flipflop_8bit_4_y5), .S0(S0), .S1(S1));
  Multiplexor_4 multiplexor_4_7 (
    .Y(multiplexor_4_7_y), .I0(flipflop_8bit_1_y6), .I1(flipflop_8bit_2_y6), .I2(flipflop_8bit_3_y6),
    .I3(flipflop_8bit_4_y6), .S0(S0), .S1(S1));
  Multiplexor_4 multiplexor_4_8 (
    .Y(multiplexor_4_8_y), .I0(flipflop_8bit_1_y7), .I1(flipflop_8bit_2_y7), .I2(flipflop_8bit_3_y7),
    .I3(flipflop_8bit_4_y7), .S0(S0), .S1(S1));
endmodule
