// Digital circuit T_FlipFlop.dig as structural Verilog
module T_FlipFlop (
  input  T,
  input  CLK,
  output out_1
);

  wire xor_1_out;

  xor xor_1 (xor_1_out, out_1, T);
  D_FlipFlop_RaisingEdge d_flipflop_raisingedge_1 (.D(xor_1_out), .CLK(CLK), .Y(out_1));
endmodule
