// Digital circuit TriState_Switch.dig as structural Verilog
module TriState_Switch (
  input  I0,
  input  Enable,
  input  I1,
  input  I2,
  input  I3,
  input  I4,
  input  I5,
  input  I6,
  input  I7,
  output Y0,
  output Y1,
  output Y2,
  output Y3,
  output Y4,
  output Y5,
  output Y6,
  output Y7
);

  wire not_1_out, not_2_out, not_3_out, not_4_out, not_5_out, not_6_out, not_7_out, not_8_out;

  not not_1 (not_1_out, Enable);
  not not_2 (not_2_out, Enable);
  not not_3 (not_3_out, Enable);
  not not_4 (not_4_out, Enable);
  not not_5 (not_5_out, Enable);
  not not_6 (not_6_out, Enable);
  not not_7 (not_7_out, Enable);
  not not_8 (not_8_out, Enable);
  TransGate transgate_1 (.A(Enable), .nA(not_1_out), .out1(I0), .out2(Y0));
  TransGate transgate_2 (.A(Enable), .nA(not_2_out), .out1(I1), .out2(Y1));
  TransGate transgate_3 (.A(Enable), .nA(not_3_out), .out1(I2), .out2(Y2));
  TransGate transgate_4 (.A(Enable), .nA(not_4_out), .out1(I3), .out2(Y3));
  TransGate transgate_5 (.A(Enable), .nA(not_5_out), .out1(I4), .out2(Y4));
  TransGate transgate_6 (.A(Enable), .nA(not_6_out), .out1(I5), .out2(Y5));
  TransGate transgate_7 (.A(Enable), .nA(not_7_out), .out1(I6), .out2(Y6));
  TransGate transgate_8 (.A(Enable), .nA(not_8_out), .out1(I7), .out2(Y7));
endmodule
