// Logisim project cpu_project.circ as structural Verilog: 14 circuits, main circuit ALU
module XOR (
  input  in_1,
  input  in_2,
  output out_3
);

  wire nand_1_out, or_1_out;

  or or_1 (or_1_out, in_2, in_1);
  nand nand_1 (nand_1_out, in_2, in_1);
  and and_1 (out_3, or_1_out, nand_1_out);
endmodule

module OR_BYNAND (
  input  in_1,
  input  in_2,
  input  in_3,
  input  in_4,
  output out_5,
  output out_6
);

  wire nand_1_out, nand_2_out;

  nand nand_1 (nand_1_out, in_1, in_1);
  nand nand_2 (nand_2_out, in_2, in_2);
  XOR xor_1 (.out_3(out_6), .in_1(in_3), .in_2(in_4));
  nand nand_3 (out_5, nand_1_out, nand_2_out);
endmodule

module AND_BYNAND (
  input  in_1,
  input  in_2,
  output out_3
);

  wire nand_1_out;

  nand nand_1 (nand_1_out, in_1, in_2);
  nand nand_2 (out_3, nand_1_out, nand_1_out);
endmodule

module XOR_BYNAND (
  input  in_1,
  input  in_2,
  output out_3
);

  wire nand_1_out, nand_2_out, nand_3_out, nand_4_out, nand_5_out;

  nand nand_1 (nand_1_out, in_1, in_1);
  nand nand_2 (nand_2_out, in_2, in_2);
  nand nand_3 (nand_3_out, nand_1_out, nand_2_out);
  nand nand_4 (nand_4_out, in_1, in_2);
  nand nand_5 (nand_5_out, nand_3_out, nand_4_out);
  nand nand_6 (out_3, nand_5_out, nand_5_out);
endmodule

module Half_adder (
  input  in_1,
  input  in_2,
  input  in_3,
  input  in_4,
  input  in_5,
  input  in_6,
  input  in_7,
  output out_8,
  output out_9,
  output out_10,
  output out_11,
  output out_12
);

  wire full_adder_1_out_5;

  and and_1 (out_9, in_1, in_2);
  xor xor_1 (out_10, in_1, in_2);
  Full_adder full_adder_1 (.in_1(in_3), .in_2(in_4), .in_3(in_5), .out_4(out_8), .out_5(full_adder_1_out_5));
  Full_adder full_adder_2 (.in_1(full_adder_1_out_5), .in_2(in_6), .in_3(in_7), .out_4(out_11), .out_5(out_12));
endmodule

module Full_adder (
  input  in_1,
  input  in_2,
  input  in_3,
  output out_4,
  output out_5
);

  wire and_1_out, and_2_out, xor_1_out;

  xor xor_1 (xor_1_out, in_1, in_2);
  and and_1 (and_1_out, xor_1_out, in_3);
  and and_2 (and_2_out, in_2, in_1);
  xor xor_2 (out_4, xor_1_out, in_3);
  or or_1 (out_5, and_1_out, and_2_out);
endmodule

module ALU (
  input  in_1,
  input  [7:0] in_2,
  input  [7:0] in_3,
  input  in_4,
  output [7:0] out_5,
  output out_6,
  output out_7
);

  wire full_adder_2_out_5, full_adder_3_out_5, full_adder_4_out_5, full_adder_5_out_5, full_adder_6_out_5,
       full_adder_7_out_5, full_adder_8_out_5;

  Full_adder full_adder_1 (.in_1(in_4), .in_2(in_4), .in_3(in_4), .out_4(out_6), .out_5(out_7));
  Full_adder full_adder_2 (.in_1(in_1), .in_2(in_2[0]), .in_3(in_3[0]), .out_4(out_5[0]), .out_5(full_adder_2_out_5));
  Full_adder full_adder_3 (
    .in_1(full_adder_2_out_5), .in_2(in_2[1]), .in_3(in_3[1]), .out_4(out_5[1]), .out_5(full_adder_3_out_5));
  Full_adder full_adder_4 (
    .in_1(full_adder_3_out_5), .in_2(in_2[2]), .in_3(in_3[2]), .out_4(out_5[2]), .out_5(full_adder_4_out_5));
  Full_adder full_adder_5 (
    .in_1(full_adder_4_out_5), .in_2(in_2[3]), .in_3(in_3[3]), .out_4(out_5[3]), .out_5(full_adder_5_out_5));
  Full_adder full_adder_6 (
    .in_1(full_adder_5_out_5), .in_2(in_2[4]), .in_3(in_3[4]), .out_4(out_5[4]), .out_5(full_adder_6_out_5));
  Full_adder full_adder_7 (
    .in_1(full_adder_6_out_5), .in_2(in_2[5]), .in_3(in_3[5]), .out_4(out_5[5]), .out_5(full_adder_7_out_5));
  Full_adder full_adder_8 (
    .in_1(full_adder_7_out_5), .in_2(in_2[6]), .in_3(in_3[6]), .out_4(out_5[6]), .out_5(full_adder_8_out_5));
  Full_adder full_adder_9 (.in_1(full_adder_8_out_5), .in_2(in_2[7]), .in_3(in_3[7]), .out_4(out_5[7]));  // open: out_5
endmodule

module latch_RS_NOR_High (
  input  in_1,
  input  in_2,
  output out_3,
  output out_4
);

  nor nor_1 (out_3, in_1, out_4);
  nor nor_2 (out_4, out_3, in_2);
endmodule

module latch_SR_NAND_LOW (
  input  in_1,
  input  in_2,
  output out_3,
  output out_4
);

  nand nand_1 (out_3, in_1, out_4);
  nand nand_2 (out_4, in_2, out_3);
endmodule

module Multiplexor_Latch (
  input  in_1,
  input  in_2,
  input  in_3,
  output out_4
);

  wire and_1_out, and_2_out, and_3_out, not_1_out;

  not not_1 (not_1_out, in_1);
  and and_1 (and_1_out, in_2, not_1_out);
  and and_2 (and_2_out, in_3, in_1);
  and and_3 (and_3_out, in_2, in_3);
  or or_1 (out_4, and_1_out, and_3_out, and_2_out);
endmodule

module Testing (
  input  in_1,
  input  in_2,
  input  in_3,
  input  in_4,
  input  in_5,
  output out_6,
  output out_7
);

  wire multiplexor_latch_1_out_4, not_1_out;

  not not_1 (not_1_out, in_1);
  Multiplexor_Latch multiplexor_latch_1 (
    .in_2(multiplexor_latch_1_out_4), .in_3(in_2), .out_4(multiplexor_latch_1_out_4), .in_1(not_1_out));
  T_FLIP_FLOP t_flip_flop_1 (.in_1(in_4), .in_2(in_5), .out_4(out_7), .in_3(in_3));
  Multiplexor_Latch multiplexor_latch_2 (.in_2(out_6), .in_3(multiplexor_latch_1_out_4), .out_4(out_6), .in_1(in_1));
endmodule

module D_Flipflop_Falling_Edge (
  input  in_1,
  input  in_2,
  output out_3,
  output out_4
);

  wire and_1_out, and_2_out, and_3_out, and_4_out, nor_1_out, nor_2_out, not_1_out, not_2_out;

  not not_1 (not_1_out, in_1);
  and and_1 (and_1_out, in_1, in_2);
  and and_2 (and_2_out, in_2, not_1_out);
  not not_2 (not_2_out, in_2);
  nor nor_1 (nor_1_out, and_1_out, nor_2_out);
  nor nor_2 (nor_2_out, nor_1_out, and_2_out);
  and and_3 (and_3_out, nor_1_out, not_2_out);
  and and_4 (and_4_out, not_2_out, nor_2_out);
  nor nor_3 (out_3, and_3_out, out_4);
  nor nor_4 (out_4, out_3, and_4_out);
endmodule

module D_Flipflop_Raising_edge (
  input  in_1,
  input  in_2,
  output out_3
);

  wire and_1_out, multiplexor_latch_1_out_4, not_1_out;

  not not_1 (not_1_out, in_2);
  and and_1 (and_1_out, out_3, 1'b1);
  Multiplexor_Latch multiplexor_latch_1 (
    .in_2(multiplexor_latch_1_out_4), .in_3(in_1), .out_4(multiplexor_latch_1_out_4), .in_1(not_1_out));
  Multiplexor_Latch multiplexor_latch_2 (
    .in_2(and_1_out), .in_3(multiplexor_latch_1_out_4), .out_4(out_3), .in_1(in_2));
endmodule

module T_FLIP_FLOP (
  input  in_1,
  input  in_2,
  input  in_3,
  output out_4
);

  wire and_1_out, xor_1_out;

  xor xor_1 (xor_1_out, out_4, in_1);
  and and_1 (and_1_out, in_3, xor_1_out);
  D_Flipflop_Raising_edge d_flipflop_raising_edge_1 (.in_1(and_1_out), .in_2(in_2), .out_3(out_4));
endmodule
